# Fritzing sketch extended wiring diagram (saved by Fritzing 0.9.3b)

parts:
  Arduino_Uno = Arduino Uno (Rev3)
  WeMos_D1_Mini2 = WeMos D1 Mini

nets:
  N1: Arduino_Uno.D0/RX, WeMos_D1_Mini2.TX
  N2: Arduino_Uno.D1/TX, WeMos_D1_Mini2.RX
  5V: Arduino_Uno.5V, WeMos_D1_Mini2.5V
  N3: Arduino_Uno.GND, WeMos_D1_Mini2.G
